# Fritzing sketch BearCon2 (saved by Fritzing 0.9.2b)
breadboards: 1

parts:
  IC1 = IC, DIP package, 52 pins [chip_label="PSOC5 CY8CKIT-059"]
  VCC1 = 4 x AAA Battery Mount
  R1 = Rotary Potentiometer (Small) [maximum_resistance=10kΩ package=THT]
  LCD1 = LCD screen
  SP1-LEFT = SPEAKER [package=pcb_mount_speaker]
  SP2-Right = SPEAKER [package=pcb_mount_speaker]
  C1 = Electrolytic Capacitor [capacitance=10µF package="100 mil [THT, electrolytic]"]
  C2 = Electrolytic Capacitor [capacitance=10µF package="100 mil [THT, electrolytic]"]
  R3 = Resistor [tolerance=±5% resistance=1k package=THT]
  LED1 = LED - 5mm [color="Red (633nm)" package="5 mm [THT]"]
  LED2 = LED - 5mm [color="Red (633nm)" package="5 mm [THT]"]
  R4 = Resistor [tolerance=±5% resistance=1k package=THT]
  RE1-TRIM = Rotary Encoder [package=THT]
  RE1-RIGHT = Rotary Encoder [package=THT]
  RE1-LEFT = Rotary Encoder [package=THT]
  S1 = SPST Switch [package=switche-dpdt]

nets:
  N1: IC1.pin2, S1.P
  N2: IC1.pin16, C1.-
  N3: IC1.pin17, C2.-
  N4: IC1.pin18, R3.Pin_0
  N5: IC1.pin19, R4.Pin_0
  N6: IC1.pin22, RE1-TRIM.EncoderPinB
  N7: IC1.pin23, RE1-TRIM.EncoderPinA
  N8: IC1.pin27, LCD1.DB4
  N9: IC1.pin28, LCD1.DB5
  N10: IC1.pin29, LCD1.DB6
  N11: IC1.pin30, LCD1.DB7
  N12: IC1.pin31, LCD1.E
  N13: IC1.pin32, LCD1.RS
  N14: IC1.pin33, LCD1.R/W
  N15: IC1.pin47, RE1-RIGHT.EncoderPinA
  N16: IC1.pin48, RE1-RIGHT.EncoderPinB
  N17: IC1.pin49, RE1-LEFT.EncoderPinA
  N18: IC1.pin50, RE1-LEFT.EncoderPinB
  GND: VCC1.-, R1.leg2, LCD1.VSS, LCD1.LED-, SP1-LEFT.-, SP2-Right.-, LED1.cathode, LED2.cathode, RE1-TRIM.EncoderPinC, RE1-RIGHT.EncoderPinC, RE1-LEFT.EncoderPinC, S1.O
  5V: VCC1.+, R1.leg1, LCD1.VDD, LCD1.LED+
  N19: R1.wiper, LCD1.V0
  N20: SP1-LEFT.+, C1.+
  N21: SP2-Right.+, C2.+
  N22: R3.Pin_1, LED1.anode
  N23: LED2.anode, R4.Pin_1
